# Fritzing sketch museumbeveiliging - eenvoudig (saved by Fritzing 0.9.3b)
breadboards: 1

parts:
  museumbeveiliging_-_eenvoudig = Arduino Uno (Rev3)
  lichtsensor = Photocell (LDR) [package=THT]
  R2 = Resistor [tolerance=±5% resistance=10k package=THT]
  alarm = Piezo Speaker
  LD1 = LD

nets:
  N1: museumbeveiliging_-_eenvoudig.A0, lichtsensor.pin_0, R2.Pin_1
  N2: museumbeveiliging_-_eenvoudig.D12/MISO, alarm.pin2
  N3: museumbeveiliging_-_eenvoudig.GND, R2.Pin_0, alarm.pin1, LD1.cathode
  N4: museumbeveiliging_-_eenvoudig.D4, LD1.anode
  N5: museumbeveiliging_-_eenvoudig.5V, lichtsensor.pin_1

custom parts:
  LD: A Generic Red Dot Laser Diode Module (~5mW)

// code stored in the sketch: museumbeveiliging - eenvoudig.ino
// de lichtsensor moet geschakeld staan tussen +5V en een analoge ingang (hier A0)
// een weerstand van 10 kilo-ohm moet geschakeld staan tussen de massa (GND) en de analoge ingang van de lichtsensor
// de twee bovenstaande onderdelen zorgen ervoor dat er een variabele spanning op A0 komt, afhankelijk van de lichtinval

// de laser moet geschakeld zijn tussen een digitale uitgang (vb. pin4) en de massa; als je de laser niet wil sturen kun je ook +5V nemen ipv pin 4
// de zoemer moet geschakeld zijn tussen een digitale uitgang (vb. pin12) en de massa

int lichtsensorPin = A0;                         // selecteer de invoerpin voor de lichtsensor
int laserPin = 4;                                // selecteer de uitvoerpin voor de laser
int omgevingslichtWaarde = 750;                  // lichtsensorWaarde met omgevingslicht
int drempelwaarde = (omgevingslichtWaarde-100);  // drempelwaarde om laseronderbreking te detecteren
int lichtmeting = 0;                             // variablee om lichtwaarde in op te slaan
int alarmPin = 12;                               // selecteer de uitvoerpin voor de zoemer

void setup() {
  pinMode(laserPin, OUTPUT);
  pinMode(alarmPin, OUTPUT);
  
}

void loop() {
  // lichtwaarde meten
  lichtmeting = analogRead(lichtsensorPin);
  digitalWrite(laserPin, HIGH);
  if(lichtmeting < (omgevingslichtWaarde-100))
  {
    digitalWrite(alarmPin, HIGH);
  }
  else
  {
    digitalWrite(alarmPin, LOW);
  }
}
